// Logisim project circuitos.circ as structural Verilog: 12 circuits, main circuit main
module main (
);

  validador validador_1 ();  // open: IN_01, in_3, WRITE__W, DUPLICATE__D, OUT_01, out_6
  enrutador_7_a_9 enrutador_7_a_9_1 ();  // open: _0, _1, _2, _3, _4, _5, _6, _7, _0_2, _1_2, _2_2, _3_2, _4_2, _5_2, _6_2, out_16, _7_2, out_18, _8, out_20, _9, out_22

  // Notes on the sheet:
  //   COORDINATOR
endmodule

module toggle (
  input  in_1,
  output out_2
);

  wire d_ff_1_q, not_1_out, xor_1_out;

  D_Flip_Flop #(.NewFFLayout("false")) d_ff_1 (.clk(xor_1_out), .D(1'b1), .Q(d_ff_1_q));  // open: Qn, preset, reset
  xor xor_1 (xor_1_out, in_1, d_ff_1_q);
  T_Flip_Flop #(.NewFFLayout("false")) t_ff_1 (.clk(not_1_out), .T(1'b1), .Q(out_2));  // open: Qn, preset, reset
  not not_1 (not_1_out, xor_1_out);
endmodule

module semaforo_transito (
  input  [1:0] in_1,
  output out_2,
  output out_3,
  output out_4
);

  wire nor_1_out, nor_4_out, not_1_out, not_2_out, not_3_out;

  not not_1 (not_1_out, in_1[1]);
  nor nor_1 (nor_1_out, not_1_out, out_4);
  nor nor_2 (out_4, in_1[1], nor_1_out);
  not not_2 (not_2_out, in_1[0]);
  nor nor_3 (out_2, not_2_out, nor_4_out);
  nor nor_4 (nor_4_out, in_1[0], out_2);
  not not_3 (not_3_out, out_4);
  and and_1 (out_3, nor_4_out, not_3_out);
endmodule

module validador (
  input  WRITE__W,
  input  IN_01,
  input  in_3,
  output DUPLICATE__D,
  output OUT_01,
  output out_6
);

  wire and_1_out, and_2_out, Retraso_out_2;

  comparador_2_bits Comparador (.in_1(IN_01), .in_3(in_3), .out_5(DUPLICATE__D), .in_2(OUT_01), .in_4(out_6));
  and and_1 (and_1_out, WRITE__W, IN_01);
  and and_2 (and_2_out, WRITE__W, in_3);
  retraso Retraso (.in_1(WRITE__W), .out_2(Retraso_out_2));
  memoria_2_bits Memoria (.in_1(and_1_out), .in_2(and_2_out), .in_3(Retraso_out_2), .out_4(OUT_01), .out_5(out_6));

  // Notes on the sheet:
  //   $$$$$
endmodule

module retraso (
  input  in_1,
  output out_2
);

  wire not_1_out;

  not not_1 (not_1_out, in_1);
  not not_2 (out_2, not_1_out);
endmodule

module memoria_2_bits (
  input  in_1,
  input  in_2,
  input  in_3,
  output out_4,
  output out_5
);

  D_Flip_Flop #(.NewFFLayout("false")) d_ff_1 (.clk(in_3), .D(in_1), .Q(out_4));  // open: Qn, preset, reset
  D_Flip_Flop #(.NewFFLayout("false")) d_ff_2 (.clk(in_3), .D(in_2), .Q(out_5));  // open: Qn, preset, reset
endmodule

module comparador_2_bits (
  input  in_1,
  input  in_2,
  input  in_3,
  input  in_4,
  output out_5
);

  wire xnor_1_out, xnor_2_out;

  xnor xnor_1 (xnor_1_out, in_1, in_2);
  and and_1 (out_5, xnor_1_out, xnor_2_out);
  xnor xnor_2 (xnor_2_out, in_3, in_4);
endmodule

module enrutador_7_a_9 (
  input  _0,
  input  _1,
  input  _2,
  input  _3,
  input  _4,
  input  _5,
  input  _6,
  input  _7,
  output _0_2,
  output _1_2,
  output _2_2,
  output _3_2,
  output _4_2,
  output _5_2,
  output _6_2,
  output out_16,
  output _7_2,
  output out_18,
  output _8,
  output out_20,
  output _9,
  output out_22
);

  or or_1 (_0_2, _0, _5);
  or or_2 (_2_2, _1, _6);
  or or_3 (_3_2, _2, _7);
  or or_4 (_5_2, _3, _4);

  assign _1_2 = _0;
  assign _4_2 = _2;
  assign _6_2 = _4;
  assign _7_2 = _5;
  assign _8 = _6;
  assign _9 = _7;
  assign out_16 = _4;
  assign out_18 = _5;
  assign out_20 = _6;
  assign out_22 = _7;

  // Notes on the sheet:
  //   Fases
  //   Semáforos
endmodule

module controlador_botones (
  output _0,
  output _1,
  output _2,
  output _3
);

  wire button_1_out, button_2_out, button_3_out, button_4_out, button_5_out, button_6_out, button_7_out,
       button_8_out, or_1_out, or_2_out, or_3_out, or_4_out, or_5_out, or_6_out, or_7_out, or_8_out;

  Button button_1 (.out(button_1_out));
  Button button_2 (.out(button_2_out));
  Button button_3 (.out(button_3_out));
  Button button_4 (.out(button_4_out));
  Button button_5 (.out(button_5_out));
  Button button_6 (.out(button_6_out));
  Button button_7 (.out(button_7_out));
  Button button_8 (.out(button_8_out));
  or or_1 (or_1_out, button_1_out, button_2_out);
  or or_2 (or_2_out, button_3_out, button_4_out);
  or or_3 (or_3_out, button_5_out, button_6_out);
  or or_4 (or_4_out, button_7_out, button_8_out);
  switch switch_1 (.in_1(or_1_out), .in_2(or_5_out), .out_3(_0));
  or or_5 (or_5_out, or_2_out, or_3_out, or_4_out);
  switch switch_2 (.in_1(or_2_out), .in_2(or_6_out), .out_3(_1));
  or or_6 (or_6_out, or_1_out, or_3_out, or_4_out);
  switch switch_3 (.in_1(or_3_out), .in_2(or_7_out), .out_3(_2));
  or or_7 (or_7_out, or_1_out, or_2_out, or_4_out);
  switch switch_4 (.in_1(or_4_out), .in_2(or_8_out), .out_3(_3));
  or or_8 (or_8_out, or_1_out, or_2_out, or_3_out);

  // Notes on the sheet:
  //   6
  //   7
  //   8
  //   9
endmodule

module switch (
  input  in_1,
  input  in_2,
  output out_3
);

  wire or_1_out;

  or or_1 (or_1_out, in_1, in_2);
  D_Flip_Flop #(.NewFFLayout("false")) d_ff_1 (.clk(or_1_out), .Q(out_3), .preset(in_1), .reset(in_2));  // open: D, Qn
endmodule

module codificador_4_a_2 (
  input  in_1,
  input  in_2,
  input  in_3,
  input  in_4,
  output out_5,
  output out_6
);

  wire and_1_out, and_2_out, and_3_out;

  and and_1 (and_1_out, ~in_1, ~in_2, in_3, ~in_4);  // AND_Gate
  and and_2 (and_2_out, ~in_1, ~in_2, ~in_3, in_4);  // AND_Gate
  and and_3 (and_3_out, ~in_1, in_2, ~in_3, ~in_4);  // AND_Gate
  or or_1 (out_5, and_1_out, and_2_out);
  or or_2 (out_6, and_2_out, and_3_out);
endmodule

module decodificador_3_a_8 (
  input  _0,
  input  _1,
  input  _2,
  output out_4,
  output out_5,
  output out_6,
  output out_7,
  output out_8,
  output out_9,
  output out_10,
  output out_11
);

  and and_1 (out_4, ~_0, ~_1, ~_2);  // AND_Gate
  and and_2 (out_5, ~_0, ~_1, _2);  // AND_Gate
  and and_3 (out_6, ~_0, _1, ~_2);  // AND_Gate
  and and_4 (out_7, ~_0, _1, _2);  // AND_Gate
  and and_5 (out_8, _0, ~_1, ~_2);  // AND_Gate
  and and_6 (out_9, _0, ~_1, _2);  // AND_Gate
  and and_7 (out_10, _0, _1, ~_2);  // AND_Gate
  and and_8 (out_11, _0, _1, _2);
endmodule
